# Fritzing sketch heart (saved by Fritzing 0.9.3b)
breadboards: 1

parts:
  Composant2 = Arduino Nano (Rev3.0)
  Q1 = NPN-Transistor [package="TO92 [THT]"]
  R3 = Resistor [tolerance=±1% resistance=50 package=THT]
  R4 = Resistor [tolerance=±5% resistance=2k package=THT]
  LED1 = LED - 5mm [color="Red (633nm)" package="5 mm [THT]"]
  LED2 = LED - 5mm [color="Red (633nm)" package="5 mm [THT]"]
  LED3 = LED - 5mm [color="Red (633nm)" package="5 mm [THT]"]
  LED4 = LED - 5mm [color="Red (633nm)" package="5 mm [THT]"]
  LED5 = LED - 5mm [color="Red (633nm)" package="5 mm [THT]"]
  LED6 = LED - 5mm [color="Red (633nm)" package="5 mm [THT]"]
  R5 = Resistor [tolerance=±1% resistance=50 package=THT]
  R6 = Resistor [tolerance=±1% resistance=50 package=THT]
  R7 = Resistor [tolerance=±1% resistance=50 package=THT]
  VCC1 = Battery
  R1 = Resistor [tolerance=±1% resistance=50 package=THT]
  R2 = Resistor [tolerance=±1% resistance=50 package=THT]

nets:
  N1: Composant2.GND, Q1.E, VCC1.-
  N2: Composant2.3V3, R3.Pin_1, R5.Pin_1, R6.Pin_1, R7.Pin_1, VCC1.+, R1.Pin_1, R2.Pin_1
  N3: Composant2.D13/SCK, R4.Pin_0
  N4: Q1.B, R4.Pin_1
  N5: Q1.C, LED1.cathode, LED2.cathode, LED3.cathode, LED4.cathode, LED5.cathode, LED6.cathode
  N6: R3.Pin_0, LED3.anode
  N7: LED1.anode, R1.Pin_0
  N8: LED2.anode, R2.Pin_0
  N9: LED4.anode, R5.Pin_0
  N10: LED5.anode, R6.Pin_0
  N11: LED6.anode, R7.Pin_0
