# Fritzing sketch heart_using_dla6srd (saved by Fritzing 0.9.3b)
breadboards: 1

parts:
  Composant2 = Arduino Nano (Rev3.0)
  Q1 = NPN-Transistor [package="TO92 [THT]"]
  R3 = Resistor [tolerance=±1% resistance=50 package=THT]
  R4 = Resistor [tolerance=±5% resistance=2k package=THT]
  R5 = Resistor [tolerance=±1% resistance=50 package=THT]
  R6 = Resistor [tolerance=±1% resistance=50 package=THT]
  R7 = Resistor [tolerance=±1% resistance=50 package=THT]
  VCC1 = Battery
  R1 = Resistor [tolerance=±1% resistance=50 package=THT]
  R2 = Resistor [tolerance=±1% resistance=50 package=THT]
  LED1 = LED - 3mm [color="Red (633nm)" package="3 mm [THT]"]
  LED2 = LED - 3mm [color="Red (633nm)" package="3 mm [THT]"]
  LED3 = LED - 3mm [color="Red (633nm)" package="3 mm [THT]"]
  LED4 = LED - 3mm [color="Red (633nm)" package="3 mm [THT]"]
  LED5 = LED - 3mm [color="Red (633nm)" package="3 mm [THT]"]
  LED6 = LED - 3mm [color="Red (633nm)" package="3 mm [THT]"]

nets:
  N1: Composant2.GND, Q1.E, VCC1.-
  N2: Composant2.3V3, VCC1.+, LED1.anode, LED2.anode, LED3.anode, LED4.anode, LED5.anode, LED6.anode
  N3: Composant2.D13/SCK, R4.Pin_0
  N4: Q1.B, R4.Pin_1
  N5: Q1.C, R3.Pin_0, R5.Pin_0, R6.Pin_0, R7.Pin_0, R1.Pin_0, R2.Pin_0
  N6: R3.Pin_1, LED5.cathode
  N7: R5.Pin_1, LED6.cathode
  N8: R6.Pin_1, LED1.cathode
  N9: R7.Pin_1, LED2.cathode
  N10: R1.Pin_1, LED4.cathode
  N11: R2.Pin_1, LED3.cathode

notes:
  On Nucleo-L011K4, the USB connector is on the left
  These 6 leds symbolize the 6 leds
  inside the DLA/6SRD
  pin 6 5 4 3 2 1
  pins 7 8 9 10 11 12
